# Fritzing sketch A4988NEMA17 (saved by Fritzing 0.9.2b)
breadboards: 1

parts:
  C1 = Electrolytic Capacitor [capacitance=100µF voltage=20V package="200 mil [THT, electrolytic]"]
  MD09B1 = A4988 Stepper Motor Driver Carrier
  M1 = Stepper Motor - Bipolar
  Onderdeel1 = Arduino Uno (Rev3)
  Power_plug1 = Power plug [part_number="PSU 12V 10A"]

nets:
  N1: C1.-, MD09B1.GROUND#141, Power_plug1.GND
  N2: C1.+, MD09B1.VMOT, Power_plug1.VCC
  N3: MD09B1.RESET, MD09B1.SLEEP
  N4: MD09B1.STEP, Onderdeel1.D13/SCK
  N5: MD09B1.DIR, Onderdeel1.D12/MISO
  N6: MD09B1.OUT_2B, M1.A
  N7: MD09B1.OUT_2A, M1.C
  N8: MD09B1.OUT_1A, M1.B
  N9: MD09B1.OUT_1B, M1.D
  VDD: MD09B1.VDD, Onderdeel1.5V
  N10: MD09B1.GROUND#147, Onderdeel1.GND
